# Fritzing sketch Camel-RaspberryPi (saved by Fritzing 0.9.1b)

parts:
  S1 = Pushbutton [package=THT]
  Raspberry_Pi = Raspberry Pi B rev2
  LED1 = LED - 5mm [color="Red (633nm)" package="5 mm [THT]"]
  R1 = Resistor [tolerance=±5% resistance=220 package=THT]

nets:
  N1: S1.leg0, Raspberry_Pi.GND, R1.Pin_0
  N2: S1.leg1, Raspberry_Pi.GPIO_18
  N3: Raspberry_Pi.GPIO_27, LED1.anode
  N4: LED1.cathode, R1.Pin_1
